# Fritzing sketch pcb (saved by Fritzing 0.9.3b)
circuit board: 30.5cm x 3.8cm
breadboards: 1

parts:
  U1 = Packages: [package=dil28-3]
  Pad4 = Pad [width=7 height=7 connect=center]  # not connected
  Pad3 = Pad [width=7 height=7 connect=center]  # not connected
  Pad2 = Pad [width=7 height=7 connect=center]  # not connected
  Pad1 = Pad [width=7 height=7 connect=center]  # not connected
  part = Pad [width=7 height=7 connect=center]  # not connected
  Pad6 = Pad [width=7 height=7 connect=center]  # not connected
  Pad7 = Pad [width=7 height=7 connect=center]  # not connected
  Pad8 = Pad [width=7 height=7 connect=center]  # not connected
  U3 = Packages: [package=dil28-3]
  R1 = Resistor [tolerance=±5% resistance=2.1k package="0603 [SMD]"]
  R3 = Resistor [tolerance=±5% resistance=2.1k package="0603 [SMD]"]
  R4 = Resistor [tolerance=±5% resistance=10k package="0402 [SMD]"]
  Pad9 = Pad [width=3.0103797777777945 height=37.723891851851846 connect=center]  # not connected
  Pad10 = Pad [width=7.902222222222222 height=5 connect=center]  # not connected
  Pad11 = Pad [width=7.902222222222222 height=5 connect=center]  # not connected
  Pad12 = Pad [width=9.3697777777777258 height=37.874222222222215 connect=center]  # not connected
  Pad13 = Pad [width=7.9000000000000004 height=5 connect=center]  # not connected
  Pad14 = Pad [width=5 height=5 connect=center]  # not connected

nets:
  N1: U1.DCPRG, U1.VCC
  N2: U1.IREF, R1.Pin_1
  N3: U1.GND, U1.VPRG, R1.Pin_0
  N4: U3.DCPRG, U3.VCC, R4.Pin_0
  N5: U3.IREF, R3.Pin_0
  N6: U3.GND, U3.VPRG, R3.Pin_1
  N7: U3.BLANK, R4.Pin_1

notes:
  o  C  D  E  +
  +
  1
  14
  15
  28
  -
  B  A  +  F  G
  o  C  D  E
