# Fritzing sketch schematics (saved by Fritzing 0.9.3b)
breadboards: 1

parts:
  TLC_5940_bottom = Packages: [package=tssop28-groundpad]
  TLC_5940_top = Packages: [package=tssop28-groundpad]
  U3 = atmega328 [package=dip]
  tenth = 7-SEGMENT-DISPLAY-1_-RED [package=7-segment-1_pth]
  one = 7-SEGMENT-DISPLAY-1_-RED [package=7-segment-1_pth]
  hundredth = 7-SEGMENT-DISPLAY-1_-RED [package=7-segment-1_pth]
  thousands = 7-SEGMENT-DISPLAY-1_-RED [package=7-segment-1_pth]
  R1 = Resistor [tolerance=±5% resistance=2.1k package=THT]
  R2 = Resistor [tolerance=±5% resistance=2.1k package=THT]
  pull_up_resistor = Resistor [tolerance=±5% resistance=10k package=THT]

nets:
  GND: TLC_5940_bottom.GND, TLC_5940_bottom.VPRG, TLC_5940_top.GND, TLC_5940_top.VPRG, U3.GND, R1.Pin_0, R2.Pin_0
  N1: TLC_5940_bottom.BLANK, TLC_5940_top.BLANK, U3.D10_(PWM), pull_up_resistor.Pin_1
  N2: TLC_5940_bottom.XLAT, TLC_5940_top.XLAT, U3.D9_(PWM)
  N3: TLC_5940_bottom.SCLK, TLC_5940_top.SCLK, U3.D13
  N4: TLC_5940_bottom.SIN, TLC_5940_top.SOUT
  N5: TLC_5940_bottom.OUT0, one.C
  N6: TLC_5940_bottom.OUT1, one.D
  N7: TLC_5940_bottom.OUT2, one.E
  N8: TLC_5940_bottom.OUT3, one.DP
  N9: TLC_5940_bottom.OUT4, tenth.C
  N10: TLC_5940_bottom.OUT5, tenth.D
  N11: TLC_5940_bottom.OUT6, tenth.E
  N12: TLC_5940_bottom.OUT7, tenth.DP
  N13: TLC_5940_bottom.OUT8, hundredth.C
  N14: TLC_5940_bottom.OUT9, hundredth.D
  N15: TLC_5940_bottom.OUT10, hundredth.E
  N16: TLC_5940_bottom.OUT11, hundredth.DP
  N17: TLC_5940_bottom.OUT12, thousands.C
  N18: TLC_5940_bottom.OUT13, thousands.D
  N19: TLC_5940_bottom.OUT14, thousands.E
  N20: TLC_5940_bottom.OUT15, thousands.DP
  N21: TLC_5940_bottom.GSCLK, TLC_5940_top.GSCLK, U3.D3_(PWM)
  5V: TLC_5940_bottom.DCPRG, TLC_5940_bottom.VCC, TLC_5940_top.DCPRG, TLC_5940_top.VCC, pull_up_resistor.Pin_0
  N22: TLC_5940_bottom.IREF, R2.Pin_1
  N23: TLC_5940_top.SIN, U3.D11_(PWM)
  N24: TLC_5940_top.OUT0, one.A
  N25: TLC_5940_top.OUT1, one.B
  N26: TLC_5940_top.OUT2, one.F
  N27: TLC_5940_top.OUT3, one.G
  N28: TLC_5940_top.OUT4, tenth.A
  N29: TLC_5940_top.OUT5, tenth.B
  N30: TLC_5940_top.OUT6, tenth.F
  N31: TLC_5940_top.OUT7, tenth.G
  N32: TLC_5940_top.OUT8, hundredth.A
  N33: TLC_5940_top.OUT9, hundredth.B
  N34: TLC_5940_top.OUT10, hundredth.F
  N35: TLC_5940_top.OUT11, hundredth.G
  N36: TLC_5940_top.OUT12, thousands.A
  N37: TLC_5940_top.OUT13, thousands.B
  N38: TLC_5940_top.OUT14, thousands.F
  N39: TLC_5940_top.OUT15, thousands.G
  N40: TLC_5940_top.IREF, R1.Pin_1
  12V: tenth.G1, one.G1, hundredth.G1, thousands.G1
